# Fritzing sketch Simultion fritzing (saved by Fritzing 0.9.3b)
breadboards: 2

parts:
  Y1 = CRYSTAL [package=hc49u-v]
  PIC16F1 = PIC16F887 [package="DIP (Dual Inline) [THT]"]
  LCD1 = LCD screen
  U1 = POT [package=pot_alpha_rv16af-20]
  R1 = Resistor [tolerance=±5% resistance=220 package="2010 [SMD]"]
  T1 = LM35 Temperature Sensor [package="TO92 [THT]"]
  U2 = Quad Comparator [part_number=LM239 package="DIP (Dual Inline) [THT]"]
  R2 = Rotary Potentiometer (Small) [maximum_resistance=100kΩ package=THT]
  Q1 = PNP-Transistor [package="TO92 [THT]"]
  Q2 = PNP-Transistor [package="TO92 [THT]"]
  R3 = Resistor [tolerance=±5% resistance=220 package="2010 [SMD]"]
  U3 = Optocoupler [package=THT]
  R4 = Resistor [tolerance=±5% resistance=1k package="2010 [SMD]"]
  U4 = RELAY [package=relay-g5q]
  D1 = Schottky Diode [part_number=1N5817 package="Melf DO-213 AB [SMD]"]
  M1 = DC Motor  # not connected
  VCC1 = Battery block 9V  # not connected

nets:
  N1: Y1.1, PIC16F1.CLKIN/OSC1/RA7
  N2: Y1.2, PIC16F1.CLKOUT/OSC2/RA6
  N3: PIC16F1.Vdd#10, LCD1.VDD, U1.A, R1.Pin_1, U2.3, R2.leg1, R2.leg2, Q2.C, U4.NC, D1.cathode
  N4: PIC16F1.Vss#11, LCD1.VSS, LCD1.R/W, LCD1.LED-, U1.E, U3.Pin_2
  N5: PIC16F1.T1CK1/T1OSO/RC0, LCD1.DB4
  N6: PIC16F1.T1CKI/T1OSO/RC1, LCD1.DB5
  N7: PIC16F1.CCP1/P1A/RC2, LCD1.DB6
  N8: PIC16F1.SCL/SCK/RC3, LCD1.DB7
  N9: PIC16F1.SDA/SDI/RC4, LCD1.RS
  N10: PIC16F1.SDO/RC5, LCD1.E
  N11: PIC16F1.INT/AN12/RB0, U2.2
  N12: LCD1.V0, U1.S
  N13: LCD1.LED+, R1.Pin_0
  N14: T1.+Vs, U3.Pin_5
  N15: T1.Vout, U2.4
  N16: T1.GND, U2.12, Q1.E
  N17: U2.5, R2.wiper
  N18: Q1.B, R4.Pin_0
  N19: Q1.C, D1.anode
  N20: Q2.E, U3.Pin_1
  N21: Q2.B, R3.Pin_0
  N22: U3.Pin_4, R4.Pin_1

custom parts:
  PIC16F887: is FLASH-based 8-bit microcontroller from Microchip with 40- pin package (8pin for Port A, 8 for Port B, 8 for Port C, 4 for Port E, 2 VDD (5v) and 2 VSS (0v).The PIC16F887 features 256 bytes of EEPROM data memory, self programming, an ICD, 2 Comparators, 14 channels of 10-bit Analog-to-Digital (A/D) converter, 1 capture/compare/PWM and 1 Enhanced capture/compare/PWM functions, a synchronous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
  Quad Comparator: LM239 Quad Comparator
